// Logisim project Associative.circ as structural Verilog: 1 circuit, main circuit main
module main (
  input  [3:0] ADDRESS
);

  wire and_1_out, and_2_out, and_3_out, and_4_out, and_5_out, and_6_out, and_7_out, and_8_out, and_9_out,
       clock_1_out, comparator_1_eq, comparator_2_eq, comparator_3_eq, comparator_4_eq, decoder_1_out0,
       decoder_1_out1, decoder_1_out2, decoder_1_out3, not_1_out, or_1_out, register_5_q, register_6_q,
       register_7_q, register_8_q;
  wire [1:0] counter_1_q;
  wire [3:0] register_1_q, register_2_q, register_3_q, register_4_q;

  Clock clock_1 (.out(clock_1_out));
  and and_1 (and_1_out, clock_1_out, not_1_out);
  Register #(.width(4)) register_1 (.D(ADDRESS), .en(and_6_out), .clk(clock_1_out), .Q(register_1_q));  // open: clr
  Register #(.width(4)) register_2 (.D(ADDRESS), .en(and_7_out), .clk(clock_1_out), .Q(register_2_q));  // open: clr
  Register #(.width(4)) register_3 (.D(ADDRESS), .en(and_8_out), .clk(clock_1_out), .Q(register_3_q));  // open: clr
  Register #(.width(4)) register_4 (.D(ADDRESS), .en(and_9_out), .clk(clock_1_out), .Q(register_4_q));  // open: clr
  Counter #(.max('h3), .width(2)) counter_1 (
    .clr(1'b0), .load(1'b0), .up(1'b1), .clk(and_1_out), .Q(counter_1_q));  // open: count, D, carry
  Comparator #(.width(4)) comparator_1 (.a(ADDRESS), .b(register_1_q), .eq(comparator_1_eq));  // open: gt, lt
  Comparator #(.width(4)) comparator_2 (.a(ADDRESS), .b(register_2_q), .eq(comparator_2_eq));  // open: gt, lt
  Comparator #(.width(4)) comparator_3 (.a(ADDRESS), .b(register_3_q), .eq(comparator_3_eq));  // open: gt, lt
  Comparator #(.width(4)) comparator_4 (.a(ADDRESS), .b(register_4_q), .eq(comparator_4_eq));  // open: gt, lt
  Register #(.width(1)) register_5 (.D(1'b1), .en(and_6_out), .clk(clock_1_out), .Q(register_5_q));  // open: clr
  Register #(.width(1)) register_6 (.D(1'b1), .en(and_7_out), .clk(clock_1_out), .Q(register_6_q));  // open: clr
  Register #(.width(1)) register_7 (.D(1'b1), .en(and_8_out), .clk(clock_1_out), .Q(register_7_q));  // open: clr
  Register #(.width(1)) register_8 (.D(1'b1), .en(and_9_out), .clk(clock_1_out), .Q(register_8_q));  // open: clr
  Decoder #(.select(2)) decoder_1 (
    .out0(decoder_1_out0), .out1(decoder_1_out1), .out2(decoder_1_out2), .out3(decoder_1_out3),
    .sel(counter_1_q));  // open: en
  and and_2 (and_2_out, register_5_q, comparator_1_eq);
  and and_3 (and_3_out, register_6_q, comparator_2_eq);
  and and_4 (and_4_out, register_7_q, comparator_3_eq);
  and and_5 (and_5_out, register_8_q, comparator_4_eq);
  and and_6 (and_6_out, decoder_1_out0, not_1_out);
  and and_7 (and_7_out, decoder_1_out1, not_1_out);
  and and_8 (and_8_out, decoder_1_out2, not_1_out);
  and and_9 (and_9_out, decoder_1_out3, not_1_out);
  or or_1 (or_1_out, and_2_out, and_3_out, and_4_out, and_5_out);
  not not_1 (not_1_out, or_1_out);
  LED HIT (.in(or_1_out));
  LED MISS (.in(not_1_out));
endmodule
