// Logisim project Direct_mapped.circ as structural Verilog: 1 circuit, main circuit main
module main (
  input  [3:0] ADDRESS
);

  wire and_1_out, clock_1_out, comparator_1_eq, decoder_1_out0, decoder_1_out1, decoder_1_out2,
       decoder_1_out3, multiplexer_2_out, not_1_out, register_5_q, register_6_q, register_7_q, register_8_q;
  wire [1:0] multiplexer_1_out, register_1_q, register_2_q, register_3_q, register_4_q;

  Clock clock_1 (.out(clock_1_out));
  Decoder #(.select(2)) decoder_1 (
    .out0(decoder_1_out0), .out1(decoder_1_out1), .out2(decoder_1_out2), .out3(decoder_1_out3));  // open: sel, en
  Register #(.width(2)) register_1 (
    .D(ADDRESS[3:2]), .en(decoder_1_out0), .clk(clock_1_out), .Q(register_1_q));  // open: clr
  Register #(.width(2)) register_2 (
    .D(ADDRESS[3:2]), .en(decoder_1_out1), .clk(clock_1_out), .Q(register_2_q));  // open: clr
  Register #(.width(2)) register_3 (
    .D(ADDRESS[3:2]), .en(decoder_1_out2), .clk(clock_1_out), .Q(register_3_q));  // open: clr
  Register #(.width(2)) register_4 (
    .D(ADDRESS[3:2]), .en(decoder_1_out3), .clk(clock_1_out), .Q(register_4_q));  // open: clr
  Multiplexer #(.select(2), .width(2)) multiplexer_1 (
    .in0(register_1_q), .in1(register_2_q), .in2(register_3_q), .in3(register_4_q), .out(multiplexer_1_out),
    .sel(ADDRESS[1:0]));
  Comparator #(.width(2)) comparator_1 (.a(ADDRESS[3:2]), .b(multiplexer_1_out), .eq(comparator_1_eq));  // open: gt, lt
  Register #(.width(1)) register_5 (.D(1'b1), .en(decoder_1_out0), .clk(clock_1_out), .Q(register_5_q));  // open: clr
  Register #(.width(1)) register_6 (.D(1'b1), .en(decoder_1_out1), .clk(clock_1_out), .Q(register_6_q));  // open: clr
  Register #(.width(1)) register_7 (.D(1'b1), .en(decoder_1_out2), .clk(clock_1_out), .Q(register_7_q));  // open: clr
  Register #(.width(1)) register_8 (.D(1'b1), .en(decoder_1_out3), .clk(clock_1_out), .Q(register_8_q));  // open: clr
  and and_1 (and_1_out, comparator_1_eq, multiplexer_2_out);
  Multiplexer #(.select(2)) multiplexer_2 (
    .in0(register_5_q), .in1(register_6_q), .in2(register_7_q), .in3(register_8_q), .out(multiplexer_2_out),
    .sel(ADDRESS[1:0]));
  not not_1 (not_1_out, and_1_out);
  LED HIT (.in(and_1_out));
  LED MISS (.in(not_1_out));
endmodule
