// Logisim project Set_Associative.circ as structural Verilog: 1 circuit, main circuit main
module main (
  input  [3:0] ADDRESS
);

  wire and_1_out, and_2_out, and_3_out, and_4_out, and_5_out, and_6_out, and_7_out, and_8_out, and_9_out,
       and_10_out, clock_1_out, comparator_1_eq, comparator_2_eq, comparator_3_eq, comparator_4_eq,
       decoder_1_out0, decoder_1_out1, multiplexer_1_out, not_1_out, not_2_out, not_3_out, or_1_out,
       or_2_out, register_5_q, register_6_q, register_7_q, register_8_q, register_9_q, register_10_q;
  wire [2:0] register_1_q, register_2_q, register_3_q, register_4_q;

  Clock clock_1 (.out(clock_1_out));
  and and_1 (and_1_out, not_3_out, and_3_out);
  and and_2 (and_2_out, register_6_q, and_3_out);
  Decoder decoder_1 (.out0(decoder_1_out0), .out1(decoder_1_out1), .sel(ADDRESS[0]));  // open: en
  and and_3 (and_3_out, decoder_1_out1, not_1_out);
  and and_4 (and_4_out, decoder_1_out0, not_1_out);
  and and_5 (and_5_out, and_4_out, not_2_out);
  Register #(.width(3)) register_1 (
    .D(ADDRESS[3:1]), .en(and_5_out), .clk(clock_1_out), .Q(register_1_q));  // open: clr
  Register #(.width(3)) register_2 (
    .D(ADDRESS[3:1]), .en(and_6_out), .clk(clock_1_out), .Q(register_2_q));  // open: clr
  Register #(.width(3)) register_3 (
    .D(ADDRESS[3:1]), .en(and_1_out), .clk(clock_1_out), .Q(register_3_q));  // open: clr
  Register #(.width(3)) register_4 (
    .D(ADDRESS[3:1]), .en(and_2_out), .clk(clock_1_out), .Q(register_4_q));  // open: clr
  and and_6 (and_6_out, and_4_out, register_5_q);
  Comparator #(.width(3)) comparator_1 (.a(register_1_q), .b(ADDRESS[3:1]), .eq(comparator_1_eq));  // open: gt, lt
  Comparator #(.width(3)) comparator_2 (.a(register_2_q), .b(ADDRESS[3:1]), .eq(comparator_2_eq));  // open: gt, lt
  Comparator #(.width(3)) comparator_3 (.a(register_3_q), .b(ADDRESS[3:1]), .eq(comparator_3_eq));  // open: gt, lt
  Comparator #(.width(3)) comparator_4 (.a(register_4_q), .b(ADDRESS[3:1]), .eq(comparator_4_eq));  // open: gt, lt
  Multiplexer multiplexer_1 (.in0(or_1_out), .in1(or_2_out), .out(multiplexer_1_out), .sel(ADDRESS[0]));
  Register #(.width(1)) register_5 (.D(not_2_out), .en(and_4_out), .clk(clock_1_out), .Q(register_5_q));  // open: clr
  Register #(.width(1)) register_6 (.D(not_3_out), .en(and_3_out), .clk(clock_1_out), .Q(register_6_q));  // open: clr
  not not_1 (not_1_out, multiplexer_1_out);
  not not_2 (not_2_out, register_5_q);
  not not_3 (not_3_out, register_6_q);
  Register #(.width(1)) register_7 (.D(1'b1), .en(and_5_out), .clk(clock_1_out), .Q(register_7_q));  // open: clr
  Register #(.width(1)) register_8 (.D(1'b1), .en(and_6_out), .clk(clock_1_out), .Q(register_8_q));  // open: clr
  Register #(.width(1)) register_9 (.D(1'b1), .en(and_1_out), .clk(clock_1_out), .Q(register_9_q));  // open: clr
  Register #(.width(1)) register_10 (.D(1'b1), .en(and_2_out), .clk(clock_1_out), .Q(register_10_q));  // open: clr
  LED HIT (.in(multiplexer_1_out));
  LED MISS (.in(not_1_out));
  and and_7 (and_7_out, register_7_q, comparator_1_eq);
  and and_8 (and_8_out, register_8_q, comparator_2_eq);
  and and_9 (and_9_out, register_9_q, comparator_3_eq);
  and and_10 (and_10_out, register_10_q, comparator_4_eq);
  or or_1 (or_1_out, and_7_out, and_8_out);
  or or_2 (or_2_out, and_9_out, and_10_out);
endmodule
